// Logisim project D Flip-Flopları ile 0-7-0 Sayacı by fatpound.circ as structural Verilog: 1 circuit, main circuit main
module main (
);

  wire A_q, A_qn, and_1_out, and_2_out, and_3_out, and_4_out, and_5_out, and_6_out, and_7_out, B_q, B_qn,
       C_q, C_qn, clock_1_out, D_q, D_qn, or_1_out, or_2_out, xor_1_out;

  Clock clock_1 (.out(clock_1_out));
  D_Flip_Flop A (.clk(clock_1_out), .D(or_2_out), .Q(A_q), .Qn(A_qn));  // open: preset, en, reset
  LED led_1 (.in(A_q));
  D_Flip_Flop B (.clk(clock_1_out), .D(or_1_out), .Q(B_q), .Qn(B_qn));  // open: preset, en, reset
  and and_1 (and_1_out, A_q, B_qn);
  LED led_2 (.in(B_q));
  and and_2 (and_2_out, B_q, C_qn);
  xor xor_1 (xor_1_out, D_q, C_q);
  and and_3 (and_3_out, B_qn, C_q, D_q);
  or or_1 (or_1_out, and_2_out, and_3_out, and_4_out);
  D_Flip_Flop C (.clk(clock_1_out), .D(xor_1_out), .Q(C_q), .Qn(C_qn));  // open: preset, en, reset
  and and_4 (and_4_out, D_qn, B_q);
  and and_5 (and_5_out, A_q, C_qn);
  LED led_3 (.in(C_q));
  D_Flip_Flop D (.clk(clock_1_out), .D(D_qn), .Q(D_q), .Qn(D_qn));  // open: preset, en, reset
  LED led_4 (.in(D_q));
  and and_6 (and_6_out, A_q, D_qn);
  and and_7 (and_7_out, A_qn, D_q, C_q, B_q);
  or or_2 (or_2_out, and_7_out, and_6_out, and_5_out, and_1_out);
endmodule
